// Digital circuit ProcessorMux.dig as structural Verilog
// Simple processor based on the MIPS architecture. 
// It is a Harvard single-cycle CPU.
// {{de Einfacher Prozessor, der an die MIPS-Architektur 
// angelehnt ist. Es handelt sich um eine Harvard 
// Single-Cycle CPU.}}
module ProcessorMux (
  input  Clock,
  input  reset,
  input  [15:0] D_in,
  output [15:0] D_out,
  output [15:0] Addr,
  output ioR,
  output ioW
);

  wire abs, ALU2D, alu_1_p5, alu_1_p6, alu_1_p7, ALUop, br, branch_1_p3, branch_1_p4, branch_1_p5, imm, ld,
       muxA, pc_hdl_1_p5, sf, src2D, st, WE;
  wire [1:0] WDmux;
  wire [2:0] muxB;
  wire [7:0] pc_hdl_1_p7;
  wire [15:0] imreg_1_p4, multiplexer_1_out, multiplexer_2_out, multiplexer_3_out, pc_hdl_1_p6,
       ramdualport_1_d, registeropt_1_p6, ROM_d, signext_1_p2, signext_1_p3, signext_1_p4;
  wire [15:8] pc_hdl_1_p7_2;

  ROM #(.AddrBits(8), .isProgramMemory("true"), .Bits(16), .Addr_Bits(16)) ROM (.A(pc_hdl_1_p7), .sel(1'b1), .D(ROM_d));
  // PC_HDL pc_hdl_1: pin names not known; wires that end beside it: Addr, Clock, abs, reset, pc_hdl_1_p5, pc_hdl_1_p6, {pc_hdl_1_p7_2, pc_hdl_1_p7}
  Multiplexer #(.Selector_Bits(2), .Bits(16)) multiplexer_1 (
    .sel(WDmux), .in_0(Addr), .in_1(ramdualport_1_d), .in_2(D_in), .in_3(pc_hdl_1_p6), .out(multiplexer_1_out));
  // ControlMux controlmux_1: pin names not known; wires that end beside it: ioR, ioW, ld, st, br, sf, ALUop, ALU2D, muxA, src2D, muxB, abs, imm, WE, ROM_d[15:9], WDmux
  // RegisterOpt registeropt_1: pin names not known; wires that end beside it: multiplexer_1_out, Clock, ROM_d[3:0], ROM_d[7:4], WE, registeropt_1_p6, D_out
  // ImReg imreg_1: pin names not known; wires that end beside it: ROM_d, imm, Clock, imreg_1_p4
  // SignExt signext_1: pin names not known; wires that end beside it: ROM_d, signext_1_p2, signext_1_p3, signext_1_p4
  Multiplexer #(.Bits(16)) multiplexer_2 (.sel(muxA), .in_0(registeropt_1_p6), .in_1(D_out), .out(multiplexer_2_out));
  Multiplexer #(.Selector_Bits(3), .Bits(16)) multiplexer_3 (
    .sel(muxB), .in_0(D_out), .in_1(imreg_1_p4), .in_2({16{1'b0}}), .in_3({16{1'b0}}), .in_4({16{1'b0}}),
    .in_5(signext_1_p2), .in_6(signext_1_p3), .in_7(signext_1_p4), .out(multiplexer_3_out));
  // Branch branch_1: pin names not known; wires that end beside it: pc_hdl_1_p5, br, branch_1_p3, branch_1_p4, branch_1_p5
  // ALU alu_1: pin names not known; wires that end beside it: multiplexer_2_out, multiplexer_3_out, branch_1_p3, Addr, alu_1_p5, alu_1_p6, alu_1_p7
  // Flags flags_1: pin names not known; wires that end beside it: branch_1_p3, branch_1_p4, branch_1_p5, ALUop, sf, Clock, alu_1_p7, alu_1_p6, alu_1_p5
  RAMDualPort #(.AddrBits(10), .Bits(16), .Addr_Bits(10)) ramdualport_1 (
    .A(Addr[9:0]), .Din(D_out), .str(st), .C(Clock), .ld(1'b1), .D(ramdualport_1_d));

  // Other names for the same wires on the sheet: C = Clock; res = reset

  // Notes on the sheet:
  //   Clock: Hz: 200
  //   reset: reset input {{de Reset Eingang}}, default 1
  //   D_in: the data input for io reads
  //   {{de Datenbus für IO Leseoperationen.}}
  //   D_out: the data output for io writes
  //   {{de Datenbus für IO Ausgaben}}
  //   Addr: the address output used for io read and write
  //   {{de Adresse für IO Operationen.}}
  //   ioR: if high, a io read is performed 
  //   {{de IO Lesefreigabe}}
  //   ioW: if high, a io write is perfromed
  //   {{de IO Schreibfreigabe}}
  //   contents of ROM (hex, n*v repeats v):
  //   802e,1220,7800,5610,5200,3c00,5e0e,3c10,640c,210,2811,6422,210,2818,6431,210,2812,
  //   6404,210,2814,640c,6a02,801a,1220,1580,1491,7359,3e90,2081,6402,1580,1491,6fe1,8026,
  //   1220,1580,8000,1390,7359,4090,2081,6403,1580,8000,1390,6fd4,8032,1220,1491,14a0,7359,
  //   3ca0,6406,3e90,8000,3b90,65c9,14a1,6fc7,4090,3c91,65c4,14a0,6fc2,8045,1220,1484,9111,
  //   1290,7359,3e90,2081,6403,1484,9111,1290,6fb5
endmodule
